// Logisim project stage1.circ as structural Verilog: 1 circuit, main circuit interface
module \interface  (
  input  _2_7,
  input  _2_6,
  input  _2_5,
  input  _2_4,
  input  _2_3,
  input  _2_2,
  input  _2_1,
  input  _2_0,
  input  _2_7_2,
  input  _2_6_2,
  input  _2_5_2,
  input  _2_4_2,
  input  _2_3_2,
  input  _2_2_2,
  input  _2_1_2,
  input  _2_0_2
);

  wire button_1_out, button_4_out, d_ff_1_q, d_ff_2_q, d_ff_3_q, d_ff_4_q, d_ff_5_q, d_ff_6_q, d_ff_7_q,
       d_ff_8_q, d_ff_9_q, d_ff_10_q, d_ff_11_q, d_ff_12_q, d_ff_13_q, d_ff_14_q, d_ff_15_q, d_ff_16_q;

  Button button_1 (.out(button_1_out));
  Button button_2 ();  // open: out
  Button button_3 ();  // open: out
  Button button_4 (.out(button_4_out));
  Button button_5 ();  // open: out
  LED led_1 ();  // open: in
  D_Flip_Flop d_ff_1 (.D(_2_7), .clk(button_1_out), .Q(d_ff_1_q), .reset(button_4_out));  // open: Qn, preset
  LED led_2 (.in(d_ff_1_q));
  D_Flip_Flop d_ff_2 (.D(_2_6), .clk(button_1_out), .Q(d_ff_2_q), .reset(button_4_out));  // open: Qn, preset
  LED led_3 (.in(d_ff_2_q));
  D_Flip_Flop d_ff_3 (.D(_2_5), .clk(button_1_out), .Q(d_ff_3_q), .reset(button_4_out));  // open: Qn, preset
  LED led_4 (.in(d_ff_3_q));
  D_Flip_Flop d_ff_4 (.D(_2_4), .clk(button_1_out), .Q(d_ff_4_q), .reset(button_4_out));  // open: Qn, preset
  D_Flip_Flop d_ff_5 (.D(_2_3), .clk(button_1_out), .Q(d_ff_5_q), .reset(button_4_out));  // open: Qn, preset
  LED led_5 (.in(d_ff_4_q));
  LED led_6 (.in(d_ff_5_q));
  D_Flip_Flop d_ff_6 (.D(_2_2), .clk(button_1_out), .Q(d_ff_6_q), .reset(button_4_out));  // open: Qn, preset
  LED led_7 (.in(d_ff_6_q));
  D_Flip_Flop d_ff_7 (.D(_2_1), .clk(button_1_out), .Q(d_ff_7_q), .reset(button_4_out));  // open: Qn, preset
  D_Flip_Flop d_ff_8 (.D(_2_0), .clk(button_1_out), .Q(d_ff_8_q), .reset(button_4_out));  // open: Qn, preset
  LED led_8 (.in(d_ff_7_q));
  LED led_9 ();  // open: in
  LED led_10 (.in(d_ff_8_q));
  LED led_11 ();  // open: in
  LED led_12 ();  // open: in
  LED led_13 ();  // open: in
  LED led_14 ();  // open: in
  Button button_6 ();  // open: out
  LED led_15 ();  // open: in
  LED led_16 ();  // open: in
  D_Flip_Flop d_ff_9 (.D(_2_7_2), .clk(button_1_out), .Q(d_ff_9_q), .reset(button_4_out));  // open: Qn, preset
  LED led_17 ();  // open: in
  LED led_18 ();  // open: in
  LED led_19 (.in(d_ff_9_q));
  LED led_20 ();  // open: in
  D_Flip_Flop d_ff_10 (.D(_2_6_2), .clk(button_1_out), .Q(d_ff_10_q), .reset(button_4_out));  // open: Qn, preset
  LED led_21 (.in(d_ff_10_q));
  D_Flip_Flop d_ff_11 (.D(_2_5_2), .clk(button_1_out), .Q(d_ff_11_q), .reset(button_4_out));  // open: Qn, preset
  LED led_22 (.in(d_ff_11_q));
  D_Flip_Flop d_ff_12 (.D(_2_4_2), .clk(button_1_out), .Q(d_ff_12_q), .reset(button_4_out));  // open: Qn, preset
  LED led_23 (.in(d_ff_12_q));
  D_Flip_Flop d_ff_13 (.D(_2_3_2), .clk(button_1_out), .Q(d_ff_13_q), .reset(button_4_out));  // open: Qn, preset
  LED led_24 (.in(d_ff_13_q));
  D_Flip_Flop d_ff_14 (.D(_2_2_2), .clk(button_1_out), .Q(d_ff_14_q), .reset(button_4_out));  // open: Qn, preset
  LED led_25 (.in(d_ff_14_q));
  D_Flip_Flop d_ff_15 (.D(_2_1_2), .clk(button_1_out), .Q(d_ff_15_q), .reset(button_4_out));  // open: Qn, preset
  LED led_26 (.in(d_ff_15_q));
  D_Flip_Flop d_ff_16 (.D(_2_0_2), .clk(button_1_out), .Q(d_ff_16_q), .reset(button_4_out));  // open: Qn, preset
  LED led_27 (.in(d_ff_16_q));

  // Notes on the sheet:
  //   Load
  //   Add
  //   Subtract
  //   Reset
  //   +/-
  //   +/-
  //   8 bit Binary Calculator
  //   Input A
  //   Input A Display
  //   +/-
  //   Output
  //   +/-
  //   +/-
  //   Input B
  //   Input B Display
endmodule
