// Logisim project stage2.circ as structural Verilog: 2 circuits, main circuit interface
module \interface  (
  input  _2_7,
  input  _2_6,
  input  _2_5,
  input  _2_4,
  input  _2_3,
  input  _2_2,
  input  _2_1,
  input  _2_0,
  input  _2_7_2,
  input  _2_6_2,
  input  _2_5_2,
  input  _2_4_2,
  input  _2_3_2,
  input  _2_2_2,
  input  _2_1_2,
  input  _2_0_2
);

  wire adderbitwandgate_1_andoutput, adderbitwandgate_1_carryout, adderbitwandgate_2_andoutput,
       adderbitwandgate_2_carryout, adderbitwandgate_3_andoutput, adderbitwandgate_3_carryout,
       adderbitwandgate_4_andoutput, adderbitwandgate_4_carryout, adderbitwandgate_5_andoutput,
       adderbitwandgate_5_carryout, adderbitwandgate_6_andoutput, adderbitwandgate_6_carryout,
       adderbitwandgate_7_andoutput, adderbitwandgate_7_carryout, and_1_out, and_2_out, button_1_out,
       button_2_out, button_4_out, c_out, d_ff_1_q, d_ff_2_q, d_ff_3_q, d_ff_4_q, d_ff_5_q, d_ff_6_q,
       d_ff_7_q, d_ff_8_q, d_ff_9_q, d_ff_10_q, d_ff_11_q, d_ff_12_q, d_ff_13_q, d_ff_14_q, d_ff_15_q,
       d_ff_16_q, s_out, t_ff_1_q, xor_1_out;

  Button button_1 (.out(button_1_out));
  Button button_2 (.out(button_2_out));
  Button button_3 ();  // open: out
  Button button_4 (.out(button_4_out));
  T_Flip_Flop t_ff_1 (.T(1'b1), .clk(button_2_out), .Q(t_ff_1_q));  // open: Qn, reset, preset
  Button button_5 ();  // open: out
  LED led_1 ();  // open: in
  D_Flip_Flop d_ff_1 (.D(_2_7), .clk(button_1_out), .Q(d_ff_1_q), .reset(button_4_out));  // open: Qn, preset
  LED led_2 (.in(d_ff_1_q));
  D_Flip_Flop d_ff_2 (.D(_2_6), .clk(button_1_out), .Q(d_ff_2_q), .reset(button_4_out));  // open: Qn, preset
  LED led_3 (.in(d_ff_2_q));
  D_Flip_Flop d_ff_3 (.D(_2_5), .clk(button_1_out), .Q(d_ff_3_q), .reset(button_4_out));  // open: Qn, preset
  LED led_4 (.in(d_ff_3_q));
  D_Flip_Flop d_ff_4 (.D(_2_4), .clk(button_1_out), .Q(d_ff_4_q), .reset(button_4_out));  // open: Qn, preset
  D_Flip_Flop d_ff_5 (.D(_2_3), .clk(button_1_out), .Q(d_ff_5_q), .reset(button_4_out));  // open: Qn, preset
  LED led_5 (.in(d_ff_4_q));
  LED led_6 (.in(d_ff_5_q));
  D_Flip_Flop d_ff_6 (.D(_2_2), .clk(button_1_out), .Q(d_ff_6_q), .reset(button_4_out));  // open: Qn, preset
  LED led_7 (.in(d_ff_6_q));
  LED led_8 (.in(adderbitwandgate_1_andoutput));
  LED led_9 ();  // open: in
  D_Flip_Flop d_ff_7 (.D(_2_1), .clk(button_1_out), .Q(d_ff_7_q), .reset(button_4_out));  // open: Qn, preset
  LED led_10 (.in(adderbitwandgate_2_andoutput));
  D_Flip_Flop d_ff_8 (.D(_2_0), .clk(button_1_out), .Q(d_ff_8_q), .reset(button_4_out));  // open: Qn, preset
  LED led_11 (.in(d_ff_7_q));
  AdderBitwANDGate adderbitwandgate_1 (
    .CarryIn(adderbitwandgate_2_carryout), .Binput(d_ff_9_q), .Ainput(d_ff_1_q), .ANDinput(t_ff_1_q),
    .CarryOut(adderbitwandgate_1_carryout), .ANDoutput(adderbitwandgate_1_andoutput));
  LED led_12 (.in(adderbitwandgate_1_carryout));
  LED led_13 (.in(adderbitwandgate_3_andoutput));
  LED led_14 (.in(adderbitwandgate_4_andoutput));
  LED led_15 (.in(d_ff_8_q));
  LED led_16 (.in(adderbitwandgate_5_andoutput));
  LED led_17 (.in(adderbitwandgate_6_andoutput));
  LED led_18 (.in(adderbitwandgate_7_andoutput));
  AdderBitwANDGate adderbitwandgate_2 (
    .CarryIn(adderbitwandgate_3_carryout), .Binput(d_ff_10_q), .Ainput(d_ff_2_q), .ANDinput(t_ff_1_q),
    .CarryOut(adderbitwandgate_2_carryout), .ANDoutput(adderbitwandgate_2_andoutput));
  LED led_19 (.in(s_out));
  Button button_6 ();  // open: out
  D_Flip_Flop d_ff_9 (.D(_2_7_2), .clk(button_1_out), .Q(d_ff_9_q), .reset(button_4_out));  // open: Qn, preset
  LED led_20 ();  // open: in
  AdderBitwANDGate adderbitwandgate_3 (
    .CarryIn(adderbitwandgate_4_carryout), .Binput(d_ff_11_q), .Ainput(d_ff_3_q), .ANDinput(t_ff_1_q),
    .CarryOut(adderbitwandgate_3_carryout), .ANDoutput(adderbitwandgate_3_andoutput));
  LED led_21 (.in(d_ff_9_q));
  D_Flip_Flop d_ff_10 (.D(_2_6_2), .clk(button_1_out), .Q(d_ff_10_q), .reset(button_4_out));  // open: Qn, preset
  LED led_22 (.in(d_ff_10_q));
  AdderBitwANDGate adderbitwandgate_4 (
    .CarryIn(adderbitwandgate_5_carryout), .Binput(d_ff_12_q), .Ainput(d_ff_4_q), .ANDinput(t_ff_1_q),
    .CarryOut(adderbitwandgate_4_carryout), .ANDoutput(adderbitwandgate_4_andoutput));
  D_Flip_Flop d_ff_11 (.D(_2_5_2), .clk(button_1_out), .Q(d_ff_11_q), .reset(button_4_out));  // open: Qn, preset
  LED led_23 (.in(d_ff_11_q));
  AdderBitwANDGate adderbitwandgate_5 (
    .CarryIn(adderbitwandgate_6_carryout), .Binput(d_ff_13_q), .Ainput(d_ff_5_q), .ANDinput(t_ff_1_q),
    .CarryOut(adderbitwandgate_5_carryout), .ANDoutput(adderbitwandgate_5_andoutput));
  D_Flip_Flop d_ff_12 (.D(_2_4_2), .clk(button_1_out), .Q(d_ff_12_q), .reset(button_4_out));  // open: Qn, preset
  LED led_24 (.in(d_ff_12_q));
  D_Flip_Flop d_ff_13 (.D(_2_3_2), .clk(button_1_out), .Q(d_ff_13_q), .reset(button_4_out));  // open: Qn, preset
  AdderBitwANDGate adderbitwandgate_6 (
    .CarryIn(adderbitwandgate_7_carryout), .Binput(d_ff_14_q), .Ainput(d_ff_6_q), .ANDinput(t_ff_1_q),
    .CarryOut(adderbitwandgate_6_carryout), .ANDoutput(adderbitwandgate_6_andoutput));
  LED led_25 (.in(d_ff_13_q));
  D_Flip_Flop d_ff_14 (.D(_2_2_2), .clk(button_1_out), .Q(d_ff_14_q), .reset(button_4_out));  // open: Qn, preset
  LED led_26 (.in(d_ff_14_q));
  AdderBitwANDGate adderbitwandgate_7 (
    .CarryIn(c_out), .Binput(d_ff_15_q), .Ainput(d_ff_7_q), .ANDinput(t_ff_1_q),
    .CarryOut(adderbitwandgate_7_carryout), .ANDoutput(adderbitwandgate_7_andoutput));
  D_Flip_Flop d_ff_15 (.D(_2_1_2), .clk(button_1_out), .Q(d_ff_15_q), .reset(button_4_out));  // open: Qn, preset
  and and_1 (and_1_out, d_ff_8_q, d_ff_16_q);
  LED led_27 (.in(d_ff_15_q));
  and and_2 (and_2_out, xor_1_out, 1'b0);
  or c (c_out, and_1_out, and_2_out);
  D_Flip_Flop d_ff_16 (.D(_2_0_2), .clk(button_1_out), .Q(d_ff_16_q), .reset(button_4_out));  // open: Qn, preset
  xor s (s_out, 1'b0, xor_1_out);
  LED led_28 (.in(d_ff_16_q));
  xor xor_1 (xor_1_out, d_ff_16_q, d_ff_8_q);

  // Notes on the sheet:
  //   Load
  //   Add
  //   Subtract
  //   Reset
  //   +/-
  //   +/-
  //   8 bit Binary Calculator
  //   Input A
  //   Input A Display
  //   +/-
  //   2^7
  //   2^6
  //   2^5
  //   2^4
  //   2^3
  //   2^1
  //   2^2
  //   2^0
  //   +/-
  //   +/-
  //   Input B
  //   Input B Display
  //   B input
  //   A input
endmodule

module AdderBitwANDGate (
  input  CarryIn,
  input  Binput,
  input  Ainput,
  input  ANDinput,
  output CarryOut,
  output ANDoutput
);

  wire and_1_out, and_2_out, xor_1_out, xor_2_out;

  and and_1 (and_1_out, Ainput, Binput);
  or or_1 (CarryOut, and_1_out, and_2_out);
  and and_2 (and_2_out, xor_1_out, CarryIn);
  xor xor_1 (xor_1_out, Binput, Ainput);
  xor xor_2 (xor_2_out, CarryIn, xor_1_out);
  and and_3 (ANDoutput, ANDinput, xor_2_out);
endmodule
