// Logisim project stage3.circ as structural Verilog: 3 circuits, main circuit interface
module \interface  (
  input  _2_7,
  input  _2_6,
  input  _2_5,
  input  _2_4,
  input  _2_3,
  input  _2_2,
  input  _2_1,
  input  _2_0,
  input  _2_7_2,
  input  _2_6_2,
  input  _2_5_2,
  input  _2_4_2,
  input  _2_3_2,
  input  _2_2_2,
  input  _2_1_2,
  input  _2_0_2
);

  wire adderbitwandgate_1_andoutsum, adderbitwandgate_1_carryout, adderbitwandgate_2_andoutsum,
       adderbitwandgate_2_carryout, adderbitwandgate_3_andoutsum, adderbitwandgate_3_carryout,
       adderbitwandgate_4_andoutsum, adderbitwandgate_4_carryout, adderbitwandgate_5_andoutsum,
       adderbitwandgate_5_carryout, adderbitwandgate_6_andoutsum, adderbitwandgate_6_carryout,
       adderbitwandgate_7_andoutsum, adderbitwandgate_7_carryout, adderbitwandgate_8_andoutsum,
       adderbitwandgate_8_carryout, adderforinverted_1_sum, adderforinverted_2_carryout,
       adderforinverted_2_sum, adderforinverted_3_carryout, adderforinverted_3_sum,
       adderforinverted_4_carryout, adderforinverted_4_sum, adderforinverted_5_carryout,
       adderforinverted_5_sum, adderforinverted_6_carryout, adderforinverted_6_sum,
       adderforinverted_7_carryout, adderforinverted_7_sum, adderforinverted_8_sum,
       adderforinverted_9_carryout, adderforinverted_9_sum, adderforinverted_10_carryout,
       adderforinverted_10_sum, adderforinverted_11_carryout, adderforinverted_11_sum,
       adderforinverted_12_carryout, adderforinverted_12_sum, adderforinverted_13_carryout,
       adderforinverted_13_sum, adderforinverted_14_carryout, adderforinverted_14_sum, and_1_out, and_2_out,
       and_3_out, and_4_out, and_5_out, and_6_out, button_1_out, button_2_out, button_4_out, button_5_out,
       button_6_out, d_ff_1_q, d_ff_2_q, d_ff_3_q, d_ff_4_q, d_ff_5_q, d_ff_6_q, d_ff_7_q, d_ff_8_q,
       d_ff_9_q, d_ff_10_q, d_ff_11_q, d_ff_12_q, d_ff_13_q, d_ff_14_q, d_ff_15_q, d_ff_16_q, or_1_out,
       or_2_out, t_ff_1_q, t_ff_2_q, t_ff_3_q, xor_1_out, xor_2_out, xor_3_out, xor_4_out, xor_5_out,
       xor_6_out, xor_7_out, xor_8_out, xor_9_out, xor_10_out, xor_11_out, xor_12_out, xor_13_out,
       xor_14_out, xor_15_out, xor_16_out, xor_17_out, xor_18_out, xor_19_out, xor_20_out;

  T_Flip_Flop t_ff_1 (.T(1'b1), .clk(button_5_out), .Q(t_ff_1_q));  // open: Qn, reset, preset
  Button button_1 (.out(button_1_out));
  Button button_2 (.out(button_2_out));
  Button button_3 ();  // open: out
  Button button_4 (.out(button_4_out));
  Button button_5 (.out(button_5_out));
  T_Flip_Flop t_ff_2 (.T(1'b1), .clk(button_2_out), .Q(t_ff_2_q));  // open: Qn, reset, preset
  D_Flip_Flop d_ff_1 (.D(_2_7), .clk(button_1_out), .Q(d_ff_1_q), .reset(button_4_out));  // open: Qn, preset
  LED led_1 (.in(t_ff_1_q));
  LED led_2 (.in(d_ff_1_q));
  D_Flip_Flop d_ff_2 (.D(_2_6), .clk(button_1_out), .Q(d_ff_2_q), .reset(button_4_out));  // open: Qn, preset
  LED led_3 (.in(d_ff_2_q));
  xor xor_1 (xor_1_out, d_ff_1_q, t_ff_1_q);
  D_Flip_Flop d_ff_3 (.D(_2_5), .clk(button_1_out), .Q(d_ff_3_q), .reset(button_4_out));  // open: Qn, preset
  xor xor_2 (xor_2_out, d_ff_2_q, t_ff_1_q);
  AdderforInverted adderforinverted_1 (
    .CarryIn(adderforinverted_2_carryout), .Binput(xor_1_out), .Ainput(1'b0), .Sum(adderforinverted_1_sum));  // open: CarryOut
  LED led_4 (.in(d_ff_3_q));
  AdderforInverted adderforinverted_2 (
    .CarryIn(adderforinverted_3_carryout), .Binput(xor_2_out), .Ainput(1'b0),
    .CarryOut(adderforinverted_2_carryout), .Sum(adderforinverted_2_sum));
  D_Flip_Flop d_ff_4 (.D(_2_4), .clk(button_1_out), .Q(d_ff_4_q), .reset(button_4_out));  // open: Qn, preset
  xor xor_3 (xor_3_out, d_ff_3_q, t_ff_1_q);
  AdderforInverted adderforinverted_3 (
    .CarryIn(adderforinverted_4_carryout), .Binput(xor_3_out), .Ainput(1'b0),
    .CarryOut(adderforinverted_3_carryout), .Sum(adderforinverted_3_sum));
  LED led_5 (.in(adderforinverted_1_sum));
  LED led_6 (.in(d_ff_4_q));
  LED led_7 (.in(adderforinverted_2_sum));
  D_Flip_Flop d_ff_5 (.D(_2_3), .clk(button_1_out), .Q(d_ff_5_q), .reset(button_4_out));  // open: Qn, preset
  xor xor_4 (xor_4_out, d_ff_4_q, t_ff_1_q);
  AdderforInverted adderforinverted_4 (
    .CarryIn(adderforinverted_5_carryout), .Binput(xor_4_out), .Ainput(1'b0),
    .CarryOut(adderforinverted_4_carryout), .Sum(adderforinverted_4_sum));
  LED led_8 (.in(adderforinverted_3_sum));
  LED led_9 (.in(adderforinverted_4_sum));
  LED led_10 (.in(d_ff_5_q));
  AdderforInverted adderforinverted_5 (
    .CarryIn(adderforinverted_6_carryout), .Binput(xor_5_out), .Ainput(1'b0),
    .CarryOut(adderforinverted_5_carryout), .Sum(adderforinverted_5_sum));
  LED led_11 (.in(adderforinverted_5_sum));
  LED led_12 (.in(adderforinverted_6_sum));
  LED led_13 (.in(adderbitwandgate_1_carryout));
  D_Flip_Flop d_ff_6 (.D(_2_2), .clk(button_1_out), .Q(d_ff_6_q), .reset(button_4_out));  // open: Qn, preset
  LED led_14 (.in(d_ff_6_q));
  xor xor_5 (xor_5_out, d_ff_5_q, t_ff_1_q);
  AdderforInverted adderforinverted_6 (
    .CarryIn(adderforinverted_7_carryout), .Binput(xor_6_out), .Ainput(1'b0),
    .CarryOut(adderforinverted_6_carryout), .Sum(adderforinverted_6_sum));
  LED led_15 (.in(adderforinverted_7_sum));
  AdderBitwANDGate adderbitwandgate_1 (
    .CarryIn(adderbitwandgate_2_carryout), .Binput(adderforinverted_8_sum), .Ainput(adderforinverted_1_sum),
    .ANDinput(t_ff_2_q), .CarryOut(adderbitwandgate_1_carryout), .ANDoutSUM(adderbitwandgate_1_andoutsum));
  D_Flip_Flop d_ff_7 (.D(_2_1), .clk(button_1_out), .Q(d_ff_7_q), .reset(button_4_out));  // open: Qn, preset
  xor xor_6 (xor_6_out, d_ff_6_q, t_ff_1_q);
  LED led_16 (.in(xor_9_out));
  LED led_17 (.in(d_ff_7_q));
  AdderforInverted adderforinverted_7 (
    .CarryIn(or_1_out), .Binput(xor_7_out), .Ainput(1'b0), .CarryOut(adderforinverted_7_carryout),
    .Sum(adderforinverted_7_sum));
  AdderBitwANDGate adderbitwandgate_2 (
    .CarryIn(adderbitwandgate_3_carryout), .Binput(adderforinverted_9_sum), .Ainput(adderforinverted_2_sum),
    .ANDinput(t_ff_2_q), .CarryOut(adderbitwandgate_2_carryout), .ANDoutSUM(adderbitwandgate_2_andoutsum));
  D_Flip_Flop d_ff_8 (.D(_2_0), .clk(button_1_out), .Q(d_ff_8_q), .reset(button_4_out));  // open: Qn, preset
  xor xor_7 (xor_7_out, d_ff_7_q, t_ff_1_q);
  and and_1 (and_1_out, xor_8_out, and_2_out);
  AdderBitwANDGate adderbitwandgate_3 (
    .CarryIn(adderbitwandgate_4_carryout), .Binput(adderforinverted_10_sum), .Ainput(adderforinverted_3_sum),
    .ANDinput(t_ff_2_q), .CarryOut(adderbitwandgate_3_carryout), .ANDoutSUM(adderbitwandgate_3_andoutsum));
  LED led_18 (.in(adderbitwandgate_1_andoutsum));
  LED led_19 (.in(adderbitwandgate_1_andoutsum));
  LED led_20 (.in(d_ff_8_q));
  xor xor_8 (xor_8_out, d_ff_8_q, t_ff_1_q);
  and and_2 (and_2_out, t_ff_1_q, 1'b1);
  and and_3 (and_3_out, xor_10_out, 1'b0);
  or or_1 (or_1_out, and_1_out, and_3_out);
  LED led_21 (.in(adderbitwandgate_2_andoutsum));
  xor xor_9 (xor_9_out, 1'b0, xor_10_out);
  AdderBitwANDGate adderbitwandgate_4 (
    .CarryIn(adderbitwandgate_5_carryout), .Binput(adderforinverted_11_sum), .Ainput(adderforinverted_4_sum),
    .ANDinput(t_ff_2_q), .CarryOut(adderbitwandgate_4_carryout), .ANDoutSUM(adderbitwandgate_4_andoutsum));
  LED led_22 (.in(adderbitwandgate_3_andoutsum));
  LED led_23 (.in(adderbitwandgate_4_andoutsum));
  Button button_6 (.out(button_6_out));
  T_Flip_Flop t_ff_3 (.T(1'b1), .clk(button_6_out), .Q(t_ff_3_q));  // open: Qn, reset, preset
  xor xor_10 (xor_10_out, and_2_out, xor_8_out);
  AdderBitwANDGate adderbitwandgate_5 (
    .CarryIn(adderbitwandgate_6_carryout), .Binput(adderforinverted_12_sum), .Ainput(adderforinverted_5_sum),
    .ANDinput(t_ff_2_q), .CarryOut(adderbitwandgate_5_carryout), .ANDoutSUM(adderbitwandgate_5_andoutsum));
  LED led_24 (.in(adderbitwandgate_5_andoutsum));
  D_Flip_Flop d_ff_9 (.D(_2_7_2), .clk(button_1_out), .Q(d_ff_9_q), .reset(button_4_out));  // open: Qn, preset
  LED led_25 (.in(t_ff_3_q));
  LED led_26 (.in(adderbitwandgate_6_andoutsum));
  LED led_27 (.in(adderbitwandgate_7_andoutsum));
  LED led_28 (.in(d_ff_9_q));
  AdderforInverted adderforinverted_8 (
    .CarryIn(adderforinverted_9_carryout), .Binput(xor_11_out), .Ainput(1'b0), .Sum(adderforinverted_8_sum));  // open: CarryOut
  AdderBitwANDGate adderbitwandgate_6 (
    .CarryIn(adderbitwandgate_7_carryout), .Binput(adderforinverted_13_sum), .Ainput(adderforinverted_6_sum),
    .ANDinput(t_ff_2_q), .CarryOut(adderbitwandgate_6_carryout), .ANDoutSUM(adderbitwandgate_6_andoutsum));
  LED led_29 (.in(adderbitwandgate_8_andoutsum));
  D_Flip_Flop d_ff_10 (.D(_2_6_2), .clk(button_1_out), .Q(d_ff_10_q), .reset(button_4_out));  // open: Qn, preset
  xor xor_11 (xor_11_out, d_ff_9_q, t_ff_3_q);
  AdderBitwANDGate adderbitwandgate_7 (
    .CarryIn(adderbitwandgate_8_carryout), .Binput(adderforinverted_14_sum), .Ainput(adderforinverted_7_sum),
    .ANDinput(t_ff_2_q), .CarryOut(adderbitwandgate_7_carryout), .ANDoutSUM(adderbitwandgate_7_andoutsum));
  LED led_30 (.in(d_ff_10_q));
  xor xor_12 (xor_12_out, d_ff_10_q, t_ff_3_q);
  AdderforInverted adderforinverted_9 (
    .CarryIn(adderforinverted_10_carryout), .Binput(xor_12_out), .Ainput(1'b0),
    .CarryOut(adderforinverted_9_carryout), .Sum(adderforinverted_9_sum));
  D_Flip_Flop d_ff_11 (.D(_2_5_2), .clk(button_1_out), .Q(d_ff_11_q), .reset(button_4_out));  // open: Qn, preset
  LED led_31 (.in(d_ff_11_q));
  AdderforInverted adderforinverted_10 (
    .CarryIn(adderforinverted_11_carryout), .Binput(xor_13_out), .Ainput(1'b0),
    .CarryOut(adderforinverted_10_carryout), .Sum(adderforinverted_10_sum));
  LED led_32 (.in(adderforinverted_8_sum));
  AdderBitwANDGate adderbitwandgate_8 (
    .CarryIn(1'b0), .Binput(xor_18_out), .Ainput(xor_9_out), .ANDinput(t_ff_2_q),
    .CarryOut(adderbitwandgate_8_carryout), .ANDoutSUM(adderbitwandgate_8_andoutsum));
  xor xor_13 (xor_13_out, d_ff_11_q, t_ff_3_q);
  AdderforInverted adderforinverted_11 (
    .CarryIn(adderforinverted_12_carryout), .Binput(xor_14_out), .Ainput(1'b0),
    .CarryOut(adderforinverted_11_carryout), .Sum(adderforinverted_11_sum));
  LED led_33 (.in(adderforinverted_9_sum));
  LED led_34 (.in(adderforinverted_10_sum));
  D_Flip_Flop d_ff_12 (.D(_2_4_2), .clk(button_1_out), .Q(d_ff_12_q), .reset(button_4_out));  // open: Qn, preset
  LED led_35 (.in(d_ff_12_q));
  AdderforInverted adderforinverted_12 (
    .CarryIn(adderforinverted_13_carryout), .Binput(xor_15_out), .Ainput(1'b0),
    .CarryOut(adderforinverted_12_carryout), .Sum(adderforinverted_12_sum));
  LED led_36 (.in(adderforinverted_11_sum));
  LED led_37 (.in(adderforinverted_12_sum));
  D_Flip_Flop d_ff_13 (.D(_2_3_2), .clk(button_1_out), .Q(d_ff_13_q), .reset(button_4_out));  // open: Qn, preset
  xor xor_14 (xor_14_out, d_ff_12_q, t_ff_3_q);
  LED led_38 (.in(adderforinverted_13_sum));
  LED led_39 (.in(d_ff_13_q));
  AdderforInverted adderforinverted_13 (
    .CarryIn(adderforinverted_14_carryout), .Binput(xor_16_out), .Ainput(1'b0),
    .CarryOut(adderforinverted_13_carryout), .Sum(adderforinverted_13_sum));
  LED led_40 (.in(adderforinverted_14_sum));
  LED led_41 (.in(xor_18_out));
  D_Flip_Flop d_ff_14 (.D(_2_2_2), .clk(button_1_out), .Q(d_ff_14_q), .reset(button_4_out));  // open: Qn, preset
  xor xor_15 (xor_15_out, d_ff_13_q, t_ff_3_q);
  AdderforInverted adderforinverted_14 (
    .CarryIn(or_2_out), .Binput(xor_17_out), .Ainput(1'b0), .CarryOut(adderforinverted_14_carryout),
    .Sum(adderforinverted_14_sum));
  LED led_42 (.in(d_ff_14_q));
  D_Flip_Flop d_ff_15 (.D(_2_1_2), .clk(button_1_out), .Q(d_ff_15_q), .reset(button_4_out));  // open: Qn, preset
  LED led_43 (.in(d_ff_15_q));
  xor xor_16 (xor_16_out, d_ff_14_q, t_ff_3_q);
  and and_4 (and_4_out, and_5_out, xor_19_out);
  D_Flip_Flop d_ff_16 (.D(_2_0_2), .clk(button_1_out), .Q(d_ff_16_q), .reset(button_4_out));  // open: Qn, preset
  xor xor_17 (xor_17_out, d_ff_15_q, t_ff_3_q);
  and and_5 (and_5_out, t_ff_3_q, 1'b1);
  and and_6 (and_6_out, xor_20_out, 1'b0);
  or or_2 (or_2_out, and_4_out, and_6_out);
  LED led_44 (.in(d_ff_16_q));
  xor xor_18 (xor_18_out, 1'b0, xor_20_out);
  xor xor_19 (xor_19_out, d_ff_16_q, t_ff_3_q);
  xor xor_20 (xor_20_out, xor_19_out, and_5_out);

  // Notes on the sheet:
  //   Load
  //   Add
  //   Subtract
  //   Reset
  //   +/-
  //   +/-
  //   Input A
  //   2^7
  //   Input A Display
  //   2^6
  //   2^5
  //   2^4
  //   2^3
  //   2^2
  //   Overflow
  //   2^1
  //   2^0
  //   +/-
  //   8 bit Binary Calculator
  //   Result Display 
  //   2^7
  //   2^6
  //   Bin
  //   2^5
  //   2^4
  //   +/-
  //   Ain
  //   2^3
  //   +/-
  //   2^1
  //   2^2
  //   Input B
  //   2^0
  //   2^7
  //   2^5
  //   2^6
  //   2^4
  //   2^3
  //   Input B Display
  //   2^2
  //   2^1
  //   2^0
  //   Bin
  //   Ain
endmodule

module AdderBitwANDGate (
  input  CarryIn,
  input  Binput,
  input  Ainput,
  input  ANDinput,
  output CarryOut,
  output ANDoutSUM
);

  wire and_1_out, and_2_out, xor_1_out, xor_2_out;

  and and_1 (and_1_out, Ainput, Binput);
  or or_1 (CarryOut, and_1_out, and_2_out);
  and and_2 (and_2_out, xor_1_out, CarryIn);
  xor xor_1 (xor_1_out, Binput, Ainput);
  xor xor_2 (xor_2_out, CarryIn, xor_1_out);
  and and_3 (ANDoutSUM, ANDinput, xor_2_out);

  // Notes on the sheet:
  //   Adder Bit with AND Gate 
  //   AND gate input for PLUS/ADD button such that when pressed only then answer is displayed on LEDs
endmodule

module AdderforInverted (
  input  CarryIn,
  input  Binput,
  input  Ainput,
  output CarryOut,
  output Sum
);

  wire and_1_out, and_2_out, xor_1_out;

  and and_1 (and_1_out, Ainput, Binput);
  or or_1 (CarryOut, and_1_out, and_2_out);
  and and_2 (and_2_out, xor_1_out, CarryIn);
  xor xor_1 (xor_1_out, Binput, Ainput);
  xor xor_2 (Sum, CarryIn, xor_1_out);
endmodule
